// Logisim project ALU.circ as structural Verilog: 4 circuits, main circuit main
module main (
  input  clk,
  input  reset,
  output [19:0] out_3,
  output [3:0] out_4,
  output [3:0] out_5,
  output [15:0] out_6,
  output [3:0] out_7,
  output [3:0] out_8,
  output [7:0] out_9,
  output out_10,
  output [15:0] out_11,
  output [7:0] out_12,
  output [15:0] out_13,
  output [7:0] out_14
);

  wire and_1_out, brach, j, memRead, memToReg, memWrite, rdSelect, regWrite;
  wire [7:0] aluOut, multiplexer_3_out, rom_2_data;
  wire [15:0] adder_1_out, adder_2_out, multiplexer_1_out, multiplexer_2_out;

  Adder #(.width(16)) adder_1 (.a(adder_2_out), .b(out_11), .out(adder_1_out), .cin(1'b0));  // open: cout
  and and_1 (and_1_out, out_10, brach);
  Multiplexer #(.width(16)) multiplexer_1 (
    .in0(adder_2_out), .in1(adder_1_out), .out(multiplexer_1_out), .sel(and_1_out), .en(1'b1));
  Multiplexer #(.width(16)) multiplexer_2 (
    .in0(multiplexer_1_out), .in1({out_3[7:4], out_3[11:8], out_3[15:12], out_3[19:16]}),
    .out(multiplexer_2_out), .sel(j), .en(1'b1));
  regfile regfile_1 (
    .clk(clk), .rs(out_3[7:4]), .regWrite(regWrite), .rt(out_3[11:8]), .rd(out_3[15:12]), .writeData(out_9),
    .readData1(out_12), .readData2(out_14));
  Register #(.width(16)) register_1 (.D(multiplexer_2_out), .Q(out_6), .clk(clk), .clr(reset));  // open: en
  Adder #(.width(16)) adder_2 (.a(out_6), .b(16'h1), .out(adder_2_out), .cin(1'b0));  // open: cout
  ROM #(.addrWidth(16), .dataWidth(20)) rom_1 (.addr(out_6), .data(out_3));  // open: sel
  Multiplexer #(.width(8)) multiplexer_3 (
    .in0(out_14), .in1(out_3[19:12]), .out(multiplexer_3_out), .sel(rdSelect), .en(1'b1));
  controller controller_1 (
    .op(out_3[3:0]), .J(j), .branch(brach), .memWrite(memWrite), .memRead(memRead), .regWrite(regWrite),
    .memToReg(memToReg), .rdSelect(rdSelect));
  ALU alu_1 (.numA(out_12), .numB(multiplexer_3_out), .aluOp(out_3[3:0]), .aluout(aluOut), .zero(out_10));
  assign out_11 = {{8{1'b0}}, {out_3[7:4], out_3[19:16]}};  // Bit_Extender bit_extender_1
  ROM rom_2 (.addr(aluOut), .data(rom_2_data));  // open: sel
  Multiplexer #(.width(8)) multiplexer_4 (.in0(aluOut), .in1(rom_2_data), .out(out_9), .sel(memToReg), .en(1'b1));

  assign out_4 = out_3[3:0];
  assign out_5 = out_3[7:4];
  assign out_7 = out_3[11:8];
  assign out_8 = out_3[15:12];
  assign out_13 = {out_3[7:4], out_3[11:8], out_3[15:12], out_3[19:16]};

  // Other names for the same wires on the sheet: brach_pc[15:0] = out_11; imm_offset[7:0] = out_3[19:12];
  //   instr[19:0] = out_3; jump_pc[15:0] = {out_3[7:4], out_3[11:8], out_3[15:12], out_3[19:16]};
  //   rd[3:0] = out_3[15:12]; rt[3:0] = out_3[11:8]; rs[3:0] = out_3[7:4]; op[3:0] = out_3[3:0]; pc[15:0] = out_6;
  //   readData1[7:0] = out_12; readData2[7:0] = out_14; writeData[7:0] = out_9; zero = out_10

  // Notes on the sheet:
  //   Input
  //   Output
  //   PC
  //   Instr Memory
  //   contents of rom_1 (hex, n*v repeats v):
  //   0 702b 1236 7030f 2045 1040f 2155 9000e 2160 2170 2180
  //   numA
  //   numB
  //   aluOp
  //   aluout
  //   Data Memory
endmodule

module ALU (
  input  [7:0] numA,
  input  [7:0] numB,
  input  [3:0] aluOp,
  output zero,
  output [7:0] aluout
);

  wire comparator_1_gt, comparator_1_lt;
  wire [2:0] bit_extender_1_out;
  wire [7:0] adder_1_out, adder_2_out, and_1_out, bit_extender_2_out, bit_extender_3_out, bit_extender_4_out,
       not_1_out, or_1_out, or_2_out, shifter_1_out, shifter_2_out, shifter_3_out, shifter_4_out,
       subtractor_1_out;

  Bit_Extender #(.out_width(3)) bit_extender_1 (.in(numB), .out(bit_extender_1_out));
  Adder adder_1 (.a(numA), .b(numB), .out(adder_1_out), .cin(1'b0));  // open: cout
  Adder adder_2 (.a(numA), .b(8'h1), .out(adder_2_out), .cin(1'b0));  // open: cout
  Subtractor subtractor_1 (.a(numA), .b(8'h1), .out(subtractor_1_out), .bin(1'b0));  // open: bout
  Comparator comparator_1 (.a(numA), .b(numB), .gt(comparator_1_gt), .eq(zero), .lt(comparator_1_lt));
  assign not_1_out = ~numA;  // NOT_Gate not_1, 8 bits wide
  assign and_1_out = numA & numB;  // AND_Gate and_1, 8 bits wide
  assign or_1_out = numA | numB;  // OR_Gate or_1, 8 bits wide
  Shifter #(.shift("lr")) shifter_1 (.in(numA), .\dist (bit_extender_1_out), .out(shifter_1_out));
  Shifter shifter_2 (.in(numA), .\dist (bit_extender_1_out), .out(shifter_2_out));
  assign bit_extender_2_out = {{7{1'b0}}, comparator_1_gt};  // Bit_Extender bit_extender_2
  assign bit_extender_3_out = {{7{1'b0}}, zero};  // Bit_Extender bit_extender_3
  assign bit_extender_4_out = {{7{1'b0}}, comparator_1_lt};  // Bit_Extender bit_extender_4
  Shifter shifter_3 (.in(bit_extender_2_out), .\dist (3'b010), .out(shifter_3_out));
  Shifter shifter_4 (.in(bit_extender_4_out), .\dist (3'b010), .out(shifter_4_out));
  assign or_2_out = shifter_3_out | bit_extender_3_out | shifter_4_out;  // OR_Gate or_2, 8 bits wide
  Multiplexer #(.select(4), .width(8)) multiplexer_1 (
    .in0(adder_1_out), .in1(adder_2_out), .in2(subtractor_1_out), .in3(or_2_out), .in4(not_1_out),
    .in5(and_1_out), .in6(or_1_out), .in7(shifter_1_out), .in8(shifter_2_out), .in9(numA), .in10(numA),
    .in11(adder_1_out), .in12(and_1_out), .in13(or_1_out), .out(aluout), .sel(aluOp), .en(1'b1));  // open: in14, in15

  // Notes on the sheet:
  //   comparison
  //   shift right
  //   shift left
  //   lw sw
  //   not
  //   and andi
  //   ori or
  //   add addi
  //   incre
  //   decre
endmodule

// Controller
module controller (
  input  [3:0] op,
  output J,
  output branch,
  output memWrite,
  output memRead,
  output regWrite,
  output memToReg,
  output rdSelect
);

  Multiplexer #(.select(4)) multiplexer_1 (
    .in0(1'b0), .in1(1'b0), .in2(1'b0), .in3(1'b0), .in4(1'b0), .in5(1'b0), .in6(1'b0), .in7(1'b0),
    .in8(1'b0), .in9(1'b0), .in10(1'b0), .in11(1'b0), .in12(1'b0), .in13(1'b0), .in14(1'b1), .in15(1'b0),
    .out(J), .sel(op), .en(1'b1));
  Multiplexer #(.select(4)) multiplexer_2 (
    .in0(1'b0), .in1(1'b0), .in2(1'b0), .in3(1'b0), .in4(1'b0), .in5(1'b0), .in6(1'b0), .in7(1'b0),
    .in8(1'b0), .in9(1'b0), .in10(1'b0), .in11(1'b0), .in12(1'b0), .in13(1'b0), .in14(1'b0), .in15(1'b1),
    .out(branch), .sel(op), .en(1'b1));
  Multiplexer #(.select(4)) multiplexer_3 (
    .in0(1'b0), .in1(1'b0), .in2(1'b0), .in3(1'b0), .in4(1'b0), .in5(1'b0), .in6(1'b0), .in7(1'b0),
    .in8(1'b0), .in9(1'b0), .in10(1'b1), .in11(1'b0), .in12(1'b0), .in13(1'b0), .in14(1'b0), .in15(1'b0),
    .out(memWrite), .sel(op), .en(1'b1));
  Multiplexer #(.select(4)) multiplexer_4 (
    .in0(1'b0), .in1(1'b0), .in2(1'b0), .in3(1'b0), .in4(1'b0), .in5(1'b0), .in6(1'b0), .in7(1'b0),
    .in8(1'b0), .in9(1'b1), .in10(1'b0), .in11(1'b0), .in12(1'b0), .in13(1'b0), .in14(1'b0), .in15(1'b0),
    .out(memRead), .sel(op), .en(1'b1));
  Multiplexer #(.select(4)) multiplexer_5 (
    .in0(1'b1), .in1(1'b1), .in2(1'b1), .in3(1'b1), .in4(1'b1), .in5(1'b1), .in6(1'b1), .in7(1'b1),
    .in8(1'b1), .in9(1'b1), .in10(1'b0), .in11(1'b1), .in12(1'b1), .in13(1'b1), .in14(1'b0), .in15(1'b0),
    .out(regWrite), .sel(op), .en(1'b1));
  Multiplexer #(.select(4)) multiplexer_6 (
    .in0(1'b0), .in1(1'b0), .in2(1'b0), .in3(1'b0), .in4(1'b0), .in5(1'b0), .in6(1'b0), .in7(1'b0),
    .in8(1'b0), .in9(1'b1), .in10(1'b0), .in11(1'b0), .in12(1'b0), .in13(1'b0), .in14(1'b0), .in15(1'b0),
    .out(memToReg), .sel(op), .en(1'b1));
  Multiplexer #(.select(4)) multiplexer_7 (
    .in0(1'b0), .in1(1'b0), .in2(1'b0), .in3(1'b0), .in4(1'b0), .in5(1'b0), .in6(1'b0), .in7(1'b0),
    .in8(1'b0), .in9(1'b1), .in10(1'b1), .in11(1'b1), .in12(1'b1), .in13(1'b1), .in14(1'b1), .in15(1'b0),
    .out(rdSelect), .sel(op), .en(1'b1));
endmodule

module regfile (
  input  clk,
  input  [3:0] rs,
  input  regWrite,
  input  [7:0] writeData,
  input  [3:0] rt,
  input  [3:0] rd,
  output [7:0] readData1,
  output [7:0] readData2
);

  wire demultiplexer_1_out0, demultiplexer_1_out1, demultiplexer_1_out2, demultiplexer_1_out3,
       demultiplexer_1_out4, demultiplexer_1_out5, demultiplexer_1_out6, demultiplexer_1_out7,
       demultiplexer_1_out8, demultiplexer_1_out9, demultiplexer_1_out10, demultiplexer_1_out11,
       demultiplexer_1_out12, demultiplexer_1_out13, demultiplexer_1_out14, demultiplexer_1_out15;
  wire [7:0] _0, _1, _2, _3, _4, _5, _6, _7, _8, _9, _10, _11, _12, _13, _14, _15, and_1_out;

  Demultiplexer #(.select(4)) demultiplexer_1 (
    .out0(demultiplexer_1_out0), .out1(demultiplexer_1_out1), .out2(demultiplexer_1_out2),
    .out3(demultiplexer_1_out3), .out4(demultiplexer_1_out4), .out5(demultiplexer_1_out5),
    .out6(demultiplexer_1_out6), .out7(demultiplexer_1_out7), .out8(demultiplexer_1_out8),
    .out9(demultiplexer_1_out9), .out10(demultiplexer_1_out10), .out11(demultiplexer_1_out11),
    .out12(demultiplexer_1_out12), .out13(demultiplexer_1_out13), .out14(demultiplexer_1_out14),
    .out15(demultiplexer_1_out15), .in(regWrite), .sel(rs), .en(1'b1));
  assign and_1_out = writeData & {8{1'b0}};  // AND_Gate and_1, 8 bits wide
  Register register_1 (.D(writeData), .en(demultiplexer_1_out1), .Q(_1), .clk(clk));  // open: clr
  Register register_2 (.D(writeData), .en(demultiplexer_1_out2), .Q(_2), .clk(clk));  // open: clr
  Register register_3 (.D(writeData), .en(demultiplexer_1_out3), .Q(_3), .clk(clk));  // open: clr
  Register register_4 (.D(writeData), .en(demultiplexer_1_out4), .Q(_4), .clk(clk));  // open: clr
  Register register_5 (.D(writeData), .en(demultiplexer_1_out5), .Q(_5), .clk(clk));  // open: clr
  Register register_6 (.D(writeData), .en(demultiplexer_1_out6), .Q(_6), .clk(clk));  // open: clr
  Register register_7 (.D(writeData), .en(demultiplexer_1_out7), .Q(_7), .clk(clk));  // open: clr
  Register register_8 (.D(writeData), .en(demultiplexer_1_out8), .Q(_8), .clk(clk));  // open: clr
  Register register_9 (.D(writeData), .en(demultiplexer_1_out9), .Q(_9), .clk(clk));  // open: clr
  Register register_10 (.D(writeData), .en(demultiplexer_1_out10), .Q(_10), .clk(clk));  // open: clr
  Register register_11 (.D(writeData), .en(demultiplexer_1_out11), .Q(_11), .clk(clk));  // open: clr
  Register register_12 (.D(writeData), .en(demultiplexer_1_out12), .Q(_12), .clk(clk));  // open: clr
  Register register_13 (.D(writeData), .en(demultiplexer_1_out13), .Q(_13), .clk(clk));  // open: clr
  Register register_14 (.D(writeData), .en(demultiplexer_1_out14), .Q(_14), .clk(clk));  // open: clr
  Register register_15 (.D(writeData), .en(demultiplexer_1_out15), .Q(_15), .clr(clk));  // open: clk
  Register register_16 (.D(and_1_out), .en(demultiplexer_1_out0), .Q(_0), .clk(clk));  // open: clr
  Multiplexer #(.select(4), .width(8)) multiplexer_1 (
    .in0(_0), .in1(_1), .in2(_2), .in3(_3), .in4(_4), .in5(_5), .in6(_6), .in7(_7), .in8(_8), .in9(_9),
    .in10(_10), .in11(_11), .in12(_12), .in13(_13), .in14(_14), .in15(_15), .out(readData1), .sel(rt),
    .en(1'b1));
  Multiplexer #(.select(4), .width(8)) multiplexer_2 (
    .in0(_0), .in1(_1), .in2(_2), .in3(_3), .in4(_4), .in5(_5), .in6(_6), .in7(_7), .in8(_8), .in9(_9),
    .in10(_10), .in11(_11), .in12(_12), .in13(_13), .in14(_14), .in15(_15), .out(readData2), .sel(rd),
    .en(1'b1));

  // Notes on the sheet:
  //   always 0
  //   $0
endmodule
